# Fritzing sketch Lego_train_1 (saved by Fritzing 0.8.7b)
breadboards: 1

parts:
  Součástka1 = Arduino Leonardo (Rev3b)
  LED1 = smd LED [color="Red (633nm)" package="0603 [SMD]"]
  VCC1 = Battery block 9V  # not connected
  M1 = DC Motor
  R1 = Resistor [tolerance=±5% resistance=220 package=THT]
  LED2 = LED - 5mm [color="Green (560nm)" package="5 mm [THT]"]
  IC1 = H-Bridge [part_number=L293DNE package=THT]
  S1 = Pushbutton [part_number=Backwards package="[THT]"]
  S2 = Pushbutton [part_number=Forwards package="[THT]"]

nets:
  N1: Součástka1.D2/SDA, IC1.1_2EN
  N2: Součástka1.D3_PWM/SCL, IC1.1A
  N3: Součástka1.D4/A6, IC1.2A
  N4: Součástka1.D7, S2.Pin_1, S2.Pin_2
  N5: Součástka1.5V, IC1.VCC1
  N6: Součástka1.GND, R1.Pin_1, S1.Pin_1, S1.Pin_2, S2.Pin_3, S2.Pin_4
  N7: Součástka1.VIN, IC1.VCC2
  N8: Součástka1.D8/A8, S1.Pin_4
  N9: Součástka1.D12/A11, LED1.cathode
  N10: Součástka1.D13_PWM, LED2.cathode
  N11: LED1.anode, R1.Pin_0, LED2.anode
  N12: M1.pin_1, IC1.2Y
  N13: M1.pin_2, IC1.1Y
